// Logisim project ex1.circ as structural Verilog: 5 circuits, main circuit NAND1
module NAND1 (
  input  I0,
  input  A1,
  input  B1,
  input  I1,
  input  sel1,
  input  sel2,
  input  I2,
  input  A2,
  input  B2,
  input  I3,
  input  A3,
  input  B3,
  input  a,
  input  sel,
  input  b,
  input  in_16,
  input  in_17,
  input  in_18,
  output RESULT,
  output out_20,
  output R2,
  output R3,
  output out_23,
  output out_24
);

  wire and_1_out, and_2_out, and_3_out, and_4_out, and_5_out, and_6_out, and_7_out, and_8_out, and_9_out,
       and_10_out, and_11_out, not_1_out, not_2_out, not_3_out, not_6_out, not_7_out, not_8_out, or_1_out,
       or_4_out, or_5_out;

  not not_1 (not_1_out, A3);
  not not_2 (not_2_out, B3);
  not not_3 (not_3_out, sel);
  Multiplexer #(.enable("false")) multiplexer_1 (.in0(in_16), .in1(in_17), .out(out_24), .sel(in_18));
  and and_1 (and_1_out, A1, B1);
  or or_1 (or_1_out, A2, B2);
  and and_2 (and_2_out, not_1_out, B3);
  and and_3 (and_3_out, A3, not_2_out);
  not not_4 (RESULT, and_1_out);
  not not_5 (R2, or_1_out);
  or or_2 (R3, and_2_out, and_3_out);
  and and_4 (and_4_out, a, not_3_out);
  and and_5 (and_5_out, sel, b);
  or or_3 (out_23, and_4_out, and_5_out);
  not not_6 (not_6_out, sel2);
  not not_7 (not_7_out, sel2);
  and and_6 (and_6_out, I0, not_6_out);
  and and_7 (and_7_out, sel2, I1);
  and and_8 (and_8_out, I2, not_7_out);
  and and_9 (and_9_out, sel2, I3);
  or or_4 (or_4_out, and_6_out, and_7_out);
  or or_5 (or_5_out, and_8_out, and_9_out);
  not not_8 (not_8_out, sel1);
  and and_10 (and_10_out, or_4_out, not_8_out);
  and and_11 (and_11_out, sel1, or_5_out);
  or or_6 (out_20, and_10_out, and_11_out);

  // Notes on the sheet:
  //   PUT CIRCUITRY HERE
endmodule

module NOR1 (
  input  A,
  input  B,
  output RESULT
);


  // Notes on the sheet:
  //   PUT CIRCUITRY HERE
endmodule

module XOR1 (
  input  A,
  input  B,
  output RESULT
);


  // Notes on the sheet:
  //   PUT CIRCUITRY HERE
endmodule

module MUX2 (
  input  A,
  input  B,
  input  Sel,
  output RESULT
);


  // Notes on the sheet:
  //   PUT CIRCUITRY HERE
endmodule

module MUX4 (
  input  A,
  input  B,
  input  C,
  input  D,
  input  Sel1,
  input  Sel2,
  output RESULT
);


  // Notes on the sheet:
  //   PUT CIRCUITRY HERE
endmodule
