// Logisim project regfile.circ as structural Verilog: 12 circuits, main circuit main
module main (
  input  [4:0] rs1,
  input  [4:0] rs2,
  input  [4:0] rd,
  input  [31:0] Write_Data,
  input  RegWEn,
  input  clk,
  output [31:0] ra,
  output [31:0] sp,
  output [31:0] t0,
  output [31:0] t1,
  output [31:0] t2,
  output [31:0] s0,
  output [31:0] s1,
  output [31:0] a0,
  output [31:0] Read_Data_1,
  output [31:0] Read_Data_2
);

  Regfile regfile_1 (
    .wri_en(RegWEn), .Rread2(rs2), .clock(clk), .write(Write_Data), .Rread1(rs1), .write_reg(rd), .R_A(ra),
    .S_P(sp), .T_0(t0), .T_1(t1), .T_2(t2), .S_0(s0), .S_1(s1), .A_0(a0), .READ2(Read_Data_2),
    .READ1(Read_Data_1));

  // Other names for the same wires on the sheet: read_data1[31:0] = Read_Data_1; read_data2[31:0] = Read_Data_2;
  //   read_reg1[4:0] = rs1; read_reg2[4:0] = rs2; write_en = RegWEn; write_reg[4:0] = rd

  // Notes on the sheet:
  //   INPUTS to your circuit
  //   DON'T CHANGE THE LOCATIONS OF THE INPUTS AND OUTPUTS!
  //   These are DEBUG/TEST outputs from your circuit.
  //   OUTPUTS from your circuit
endmodule

module RA (
  input  [31:0] in_1,
  input  WE,
  input  CLK,
  output [31:0] out_4
);

  Register #(.width(32)) register_1 (.D(in_1), .en(WE), .clk(CLK), .Q(out_4));  // open: clr
endmodule

module SP (
  input  [31:0] in_1,
  input  WE,
  input  CLK,
  output [31:0] out_4
);

  Register #(.width(32)) register_1 (.D(in_1), .en(WE), .clk(CLK), .Q(out_4));  // open: clr
endmodule

module T0 (
  input  [31:0] in_1,
  input  WE,
  input  CLK,
  output [31:0] out_4
);

  Register #(.width(32)) register_1 (.D(in_1), .en(WE), .clk(CLK), .Q(out_4));  // open: clr
endmodule

module T1 (
  input  [31:0] in_1,
  input  WE,
  input  CLk,
  output [31:0] out_4
);

  Register #(.width(32)) register_1 (.D(in_1), .en(WE), .clk(CLk), .Q(out_4));  // open: clr
endmodule

module T2 (
  input  [31:0] in_1,
  input  WE,
  input  CLK,
  output [31:0] out_4
);

  Register #(.width(32)) register_1 (.D(in_1), .en(WE), .clk(CLK), .Q(out_4));  // open: clr
endmodule

module S0 (
  input  [31:0] in_1,
  input  WE,
  input  CLk,
  output [31:0] out_4
);

  Register #(.width(32)) register_1 (.D(in_1), .en(WE), .clk(CLk), .Q(out_4));  // open: clr
endmodule

module S1 (
  input  [31:0] in_1,
  input  WE,
  input  CLk,
  output [31:0] out_4
);

  Register #(.width(32)) register_1 (.D(in_1), .en(WE), .clk(CLk), .Q(out_4));  // open: clr
endmodule

module A0 (
  input  [31:0] in_1,
  input  WE,
  input  CLK,
  output [31:0] out_4
);

  Register #(.width(32)) register_1 (.D(in_1), .en(WE), .clk(CLK), .Q(out_4));  // open: clr
endmodule

module X0 (
  input  in_1,
  output [31:0] out_2
);

  Register #(.width(32)) register_1 (.D({32{1'b0}}), .clk(in_1), .Q(out_2));  // open: en, clr
endmodule

module Regfile (
  input  wri_en,
  input  [4:0] Rread2,
  input  clock,
  input  [31:0] write,
  input  [4:0] Rread1,
  input  [4:0] write_reg,
  output [31:0] R_A,
  output [31:0] S_P,
  output [31:0] T_0,
  output [31:0] T_1,
  output [31:0] T_2,
  output [31:0] S_0,
  output [31:0] S_1,
  output [31:0] A_0,
  output [31:0] READ2,
  output [31:0] READ1
);

  wire [3:0] bit_extender_2_out;
  wire [10:0] bit_extender_1_out, shifter_1_out;
  wire [31:0] demultiplexer_1_out1, demultiplexer_1_out2, demultiplexer_1_out5, demultiplexer_1_out6,
       demultiplexer_1_out7, demultiplexer_1_out8, demultiplexer_1_out9, demultiplexer_1_out10, x0_1_out_2;

  assign bit_extender_1_out = {{10{1'b0}}, wri_en};  // Bit_Extender bit_extender_1
  Bit_Extender #(.in_width(5), .out_width(4), .\type ("zero")) bit_extender_2 (
    .in(write_reg), .out(bit_extender_2_out));
  Shifter #(.width(11)) shifter_1 (.in(bit_extender_1_out), .\dist (bit_extender_2_out), .out(shifter_1_out));
  X0 x0_1 (.in_1(clock), .out_2(x0_1_out_2));
  Demultiplexer #(.select(5), .width(32), .enable("false")) demultiplexer_1 (
    .out1(demultiplexer_1_out1), .out2(demultiplexer_1_out2), .out5(demultiplexer_1_out5),
    .out6(demultiplexer_1_out6), .out7(demultiplexer_1_out7), .out8(demultiplexer_1_out8),
    .out9(demultiplexer_1_out9), .out10(demultiplexer_1_out10), .in(write), .sel(write_reg));  // open: out0, out3, out4, out11, out12, out13, out14, out15, out16, out17, out18, out19, out20, out21, out22, out23, out24, out25, out26, out27, out28, out29, out30, out31
  RA ra_1 (.in_1(demultiplexer_1_out1), .WE(shifter_1_out[1]), .CLK(clock), .out_4(R_A));
  SP sp_1 (.in_1(demultiplexer_1_out2), .WE(shifter_1_out[2]), .CLK(clock), .out_4(S_P));
  T0 t0_1 (.in_1(demultiplexer_1_out5), .WE(shifter_1_out[5]), .CLK(clock), .out_4(T_0));
  T1 t1_1 (.in_1(demultiplexer_1_out6), .WE(shifter_1_out[6]), .CLk(clock), .out_4(T_1));
  T2 t2_1 (.in_1(demultiplexer_1_out7), .WE(shifter_1_out[7]), .CLK(clock), .out_4(T_2));
  S0 s0_1 (.in_1(demultiplexer_1_out8), .WE(shifter_1_out[8]), .CLk(clock), .out_4(S_0));
  S1 s1_1 (.in_1(demultiplexer_1_out9), .WE(shifter_1_out[9]), .CLk(clock), .out_4(S_1));
  A0 a0_1 (.in_1(demultiplexer_1_out10), .WE(shifter_1_out[10]), .CLK(clock), .out_4(A_0));
  Multiplexer #(.select(5), .width(32), .enable("false")) multiplexer_1 (
    .in0(x0_1_out_2), .in1(R_A), .in2(S_P), .in5(T_0), .in6(T_1), .in7(T_2), .in8(S_0), .in9(S_1),
    .in10(A_0), .out(READ1), .sel(Rread1));  // open: in3, in4, in11, in12, in13, in14, in15, in16, in17, in18, in19, in20, in21, in22, in23, in24, in25, in26, in27, in28, in29, in30, in31
  Multiplexer #(.select(5), .width(32), .enable("false")) multiplexer_2 (
    .in0(x0_1_out_2), .in1(R_A), .in2(S_P), .in5(T_0), .in6(T_1), .in7(T_2), .in8(S_0), .in9(S_1),
    .in10(A_0), .out(READ2), .sel(Rread2));  // open: in3, in4, in11, in12, in13, in14, in15, in16, in17, in18, in19, in20, in21, in22, in23, in24, in25, in26, in27, in28, in29, in30, in31
endmodule

module test (
  input  [31:0] in_1,
  input  in_2,
  input  in_3,
  output [31:0] out_4
);

  RA ra_1 (.in_1(in_1), .WE(in_2), .CLK(in_3), .out_4(out_4));
endmodule
